// Logisim project CPU.circ as structural Verilog: 4 circuits, main circuit main
module main (
);

  wire cpu_1_out_11, cpu_1_out_13, cpu_1_out_15, cpu_1_out_16, cpu_1_out_17, cpu_1_out_18, cpu_1_out_19,
       cpu_1_out_20, cpu_1_out_21, cpu_1_out_22, Hard_Drive_out_1, Hard_Drive_out_2, Hard_Drive_out_3,
       Hard_Drive_out_4, Hard_Drive_out_5, Hard_Drive_out_6, Hard_Drive_out_7, Hard_Drive_out_8,
       Hard_Drive_out_9, Hard_Drive_out_10, Hard_Drive_out_11, Hard_Drive_out_12, Monitor_out_1,
       Monitor_out_2, Monitor_out_3, Monitor_out_4;

  External_Device Hard_Drive (
    .out_1(Hard_Drive_out_1), .out_2(Hard_Drive_out_2), .out_3(Hard_Drive_out_3), .out_4(Hard_Drive_out_4),
    .out_5(Hard_Drive_out_5), .out_6(Hard_Drive_out_6), .out_7(Hard_Drive_out_7), .out_8(Hard_Drive_out_8),
    .out_9(Hard_Drive_out_9), .out_10(Hard_Drive_out_10), .out_11(Hard_Drive_out_11),
    .out_12(Hard_Drive_out_12));
  External_Device Monitor (
    .out_1(Monitor_out_1), .out_2(Monitor_out_2), .out_3(Monitor_out_3), .out_4(Monitor_out_4),
    .out_5(Hard_Drive_out_5), .out_6(Hard_Drive_out_6), .out_7(Hard_Drive_out_7), .out_8(Hard_Drive_out_8),
    .out_9(Hard_Drive_out_9), .out_10(Hard_Drive_out_10), .out_11(Hard_Drive_out_11),
    .out_12(Hard_Drive_out_12));
  External_Device Keyboard (
    .out_1(Hard_Drive_out_4), .out_2(Hard_Drive_out_3), .out_3(Hard_Drive_out_2), .out_4(Hard_Drive_out_1),
    .out_5(Hard_Drive_out_5), .out_6(Hard_Drive_out_6), .out_7(Hard_Drive_out_7), .out_8(Hard_Drive_out_8),
    .out_9(Hard_Drive_out_9), .out_10(Hard_Drive_out_10), .out_11(Hard_Drive_out_11),
    .out_12(Hard_Drive_out_12));
  CPU cpu_1 (
    .out_11(cpu_1_out_11), .out_13(cpu_1_out_13), .out_9(Monitor_out_1), .out_10(Monitor_out_2),
    .out_12(Monitor_out_3), .out_14(Monitor_out_4), .out_15(cpu_1_out_15), .out_16(cpu_1_out_16),
    .out_17(cpu_1_out_17), .out_18(cpu_1_out_18), .out_19(cpu_1_out_19), .out_20(cpu_1_out_20),
    .out_21(cpu_1_out_21), .out_22(cpu_1_out_22), .out_1(Hard_Drive_out_12), .out_2(Hard_Drive_out_11),
    .out_3(Hard_Drive_out_10), .out_4(Hard_Drive_out_9), .out_5(Hard_Drive_out_8), .out_6(Hard_Drive_out_7),
    .out_7(Hard_Drive_out_6), .out_8(Hard_Drive_out_5));
  RAM RAM (
    .out_1(cpu_1_out_15), .out_2(cpu_1_out_16), .out_3(cpu_1_out_17), .out_4(cpu_1_out_18),
    .out_5(cpu_1_out_19), .out_6(cpu_1_out_20), .out_7(cpu_1_out_21), .out_8(cpu_1_out_22),
    .out_9(cpu_1_out_11), .out_10(cpu_1_out_13), .out_11(Hard_Drive_out_5), .out_12(Hard_Drive_out_6),
    .out_13(Hard_Drive_out_7), .out_14(Hard_Drive_out_8), .out_15(Hard_Drive_out_9),
    .out_16(Hard_Drive_out_10), .out_17(Hard_Drive_out_11), .out_18(Hard_Drive_out_12));

  // Notes on the sheet:
  //   Control Bus
  //   Address Bus
  //   Data Bus
  //   Set
  //   Enable
endmodule

module CPU (
  output out_1,
  output out_2,
  output out_3,
  output out_4,
  output out_5,
  output out_6,
  output out_7,
  output out_8,
  output out_9,
  output out_10,
  output out_11,
  output out_12,
  output out_13,
  output out_14,
  output out_15,
  output out_16,
  output out_17,
  output out_18,
  output out_19,
  output out_20,
  output out_21,
  output out_22
);
endmodule

module External_Device (
  output out_1,
  output out_2,
  output out_3,
  output out_4,
  output out_5,
  output out_6,
  output out_7,
  output out_8,
  output out_9,
  output out_10,
  output out_11,
  output out_12
);
endmodule

module RAM (
  output out_1,
  output out_2,
  output out_3,
  output out_4,
  output out_5,
  output out_6,
  output out_7,
  output out_8,
  output out_9,
  output out_10,
  output out_11,
  output out_12,
  output out_13,
  output out_14,
  output out_15,
  output out_16,
  output out_17,
  output out_18
);
endmodule
